// Logisim project selects.circ as structural Verilog: 1 circuit, main circuit main
module main (
  input  ROMS,
  input  A0,
  input  A1,
  input  SIZ0,
  input  SIZ1,
  output UUDS,
  output UMDS,
  output LMDS,
  output LLDS
);

  wire and_1_out, and_2_out, and_3_out, and_4_out, and_5_out, and_6_out, and_7_out, and_8_out, and_9_out,
       and_10_out, and_11_out, and_12_out, not_1_out, not_2_out, not_3_out, not_4_out, not_5_out, not_6_out,
       not_7_out, not_8_out, or_1_out, or_2_out, or_3_out, or_4_out;

  not not_1 (not_1_out, A0);
  not not_2 (not_2_out, A1);
  not not_3 (not_3_out, SIZ0);
  not not_4 (not_4_out, SIZ1);
  and and_1 (and_1_out, not_1_out, not_2_out);
  and and_2 (and_2_out, not_3_out, not_2_out);
  and and_3 (and_3_out, not_2_out, A0);
  and and_4 (and_4_out, SIZ1, not_2_out);
  and and_5 (and_5_out, not_1_out, A1);
  and and_6 (and_6_out, not_2_out, not_3_out, not_4_out);
  and and_7 (and_7_out, SIZ1, SIZ0, not_2_out);
  and and_8 (and_8_out, not_3_out, not_2_out, A0);
  and and_9 (and_9_out, A0, SIZ0, SIZ1);
  and and_10 (and_10_out, not_3_out, not_4_out);
  and and_11 (and_11_out, A0, A1);
  and and_12 (and_12_out, A1, SIZ1);
  or or_1 (or_1_out, and_1_out, 1'b0);
  or or_2 (or_2_out, and_2_out, and_3_out, and_4_out, 1'b0);
  or or_3 (or_3_out, and_5_out, and_6_out, 1'b0, and_7_out, and_8_out);
  or or_4 (or_4_out, and_9_out, and_10_out, 1'b0, and_11_out, and_12_out);
  not not_5 (not_5_out, or_1_out);
  not not_6 (not_6_out, or_2_out);
  not not_7 (not_7_out, or_3_out);
  not not_8 (not_8_out, or_4_out);
  or or_5 (UUDS, not_5_out, ROMS);
  or or_6 (UMDS, ROMS, not_6_out);
  or or_7 (LMDS, not_7_out, ROMS);
  or or_8 (LLDS, not_8_out, ROMS);
endmodule
